# Fritzing sketch rfid_oled_nodemcu (saved by Fritzing 0.9.10b)

parts:
  Mod1 = Amica NodeMCU DEVKIT 1.0
  Parça1 = RFID-RC522-v2
  OLED_I2C1 = OLED 128x64 I2C Monochrome Display
  J1 = Power Jack [package=power_jack_pth]
  LED1 = LED - 3mm [color="Red (633nm)" current=0.030 package="3 mm [THT]"]
  LED2 = LED - 3mm [color="Green (570nm)" current=0.030 package="3 mm [THT]"]
  J2 = Piezo Speaker
  R1 = Resistor [tolerance=±5% resistance=220 package="0603 [SMD]"]  # not connected
  R2 = Resistor [tolerance=±5% resistance=220 package="0603 [SMD]"]  # not connected

nets:
  3.3V: Mod1.pin1, Mod1.pin_10, Mod1.pin_26, Parça1.3.3V, OLED_I2C1.VDD
  GND: Mod1.pin2, Mod1.pin_9, Mod1.pin_25, Mod1.pin_29, Parça1.GND, OLED_I2C1.GND, J1.GNDBREAK, J2.pin1
  N1: Mod1.pin6, Parça1.MOSI
  N2: Mod1.pin7, Parça1.MISO
  N3: Mod1.pin8, Parça1.SCK
  N4: Mod1.pin_12, Parça1.SDA
  N5: Mod1.pin_13, OLED_I2C1.SDA
  N6: Mod1.pin_14, OLED_I2C1.SCK
  N7: Mod1.pin_15, Parça1.RST
  N8: Mod1.pin_19, LED2.anode
  N9: Mod1.pin_20, LED1.anode
  N10: Mod1.pin_21, J2.pin2
  N11: Mod1.pin_30, J1.PWR

custom parts:
  RFID-RC522-v2: A simple China made RFID-RC522 Reader; do check the pin labels, as this is a MFRC522 based clone.
